# Fritzing sketch SalidaPWM_led (saved by Fritzing 0.9.3b)
breadboards: 1

parts:
  R2 = Resistor [tolerance=±5% resistance=10k package=THT]
  Q1_NPN = NPN-Transistor [part_number="S8050 E-B-C" package="TO92 [THT]"]
  LED1 = Super Flux LED blue [color=Blue]
  VCC1 = Battery block 9V
  R4 = Resistor [tolerance=±5% resistance=1k package=THT]
  Pico = Raspberry Pi Pico
  R3 = Resistor [tolerance=±5% resistance=220 package=THT]
  BAT_3_7v = Battery Holders [package=lipo-1100mAh]

nets:
  N1: R2.Pin_0, Q1_NPN.B, R4.Pin_0
  N2: R2.Pin_1, Q1_NPN.E, VCC1.-, Pico.pin_3, Pico.pin_8, Pico.pin_13, Pico.pin_18, Pico.pin_23, Pico.pin_28, Pico.pin_33, Pico.pin_38, Pico.pin_42, BAT_3_7v.-
  N3: Q1_NPN.C, LED1.cathode
  N4: LED1.anode, R3.Pin_1
  N5: VCC1.+, R3.Pin_0
  N6: R4.Pin_1, Pico.pin_20
  N7: Pico.pin_39, BAT_3_7v.+

custom parts:
  Raspberry Pi Pico: Raspberry Pi Pico. Based around the RP2040 microcontroller the Pico is a low cost microcontroller device bringing Raspberry Pi quality, cost, and easy of use to the microcontroller space. Jan 2021, Split part in to two versions: tht (this one) and SMD. This one will drill holes for a .1 in header in pcb to allow plugging in the module as well as providing pads to solder the module to the top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
